// Digital circuit 8bit-PC.dig as structural Verilog
module _8bit_PC (
  input  clk,
  input  [1:0] ctrl,
  input  [7:0] Inc_by,
  input  [7:0] ManualJump_val,
  output [7:0] \output 
);

  wire [7:0] _8bitripplecarryadder_1_p4, multiplexer_1_out;

  // _8bitripplecarryadder _8bitripplecarryadder_1: pin names not known; wires that end beside it: Inc_by, \output , 1'b0, _8bitripplecarryadder_1_p4
  Multiplexer #(.Selector_Bits(2), .Bits(8)) multiplexer_1 (
    .sel(ctrl), .in_0(ManualJump_val), .in_1(_8bitripplecarryadder_1_p4), .in_2({8{1'b0}}), .in_3({8{1'b1}}),
    .out(multiplexer_1_out));
  D_FF d_ff_1 (.D(multiplexer_1_out[7]), .C(clk), .Q(\output [7]));  // open: nQ
  D_FF d_ff_2 (.D(multiplexer_1_out[6]), .C(clk), .Q(\output [6]));  // open: nQ
  D_FF d_ff_3 (.D(multiplexer_1_out[5]), .C(clk), .Q(\output [5]));  // open: nQ
  D_FF d_ff_4 (.D(multiplexer_1_out[4]), .C(clk), .Q(\output [4]));  // open: nQ
  D_FF d_ff_5 (.D(multiplexer_1_out[3]), .C(clk), .Q(\output [3]));  // open: nQ
  D_FF d_ff_6 (.D(multiplexer_1_out[2]), .C(clk), .Q(\output [2]));  // open: nQ
  D_FF d_ff_7 (.D(multiplexer_1_out[1]), .C(clk), .Q(\output [1]));  // open: nQ
  D_FF d_ff_8 (.D(multiplexer_1_out[0]), .C(clk), .Q(\output [0]));  // open: nQ

  // Notes on the sheet:
  //   ctrl: 00->Load
  //   01->INC
  //   10->Reset
  //   11->Set FF
  //   ctrl signals:
  //   00->Load
  //   01->Increment
  //   10->Reset
  //   11->Set FF
  //   The 8-bit Register
  //   Matthew's 8-bit PC implementation
endmodule
