// Digital circuit 8bitgeneralregister.dig as structural Verilog
module _8bitgeneralregister (
  input  [1:0] ctrl,
  input  clk,
  input  [1:0] RegisterSelection,
  input  [7:0] Input,
  output [7:0] Output
);

  wire and_1_out, and_2_out, and_3_out, and_4_out, decoder_1_out_0, decoder_1_out_1, decoder_1_out_2,
       decoder_1_out_3;
  wire [7:0] R_0_output, R_1_output, R_2_output, R_3_output;

  Decoder #(.Selector_Bits(2)) decoder_1 (
    .sel(RegisterSelection), .out_0(decoder_1_out_0), .out_1(decoder_1_out_1), .out_2(decoder_1_out_2),
    .out_3(decoder_1_out_3));
  and and_1 (and_1_out, clk, decoder_1_out_0);
  and and_2 (and_2_out, clk, decoder_1_out_1);
  and and_3 (and_3_out, clk, decoder_1_out_2);
  and and_4 (and_4_out, clk, decoder_1_out_3);
  _8_bit_register R_0 (.clk(and_1_out), .Input(Input), .ctrl(ctrl), .\output (R_0_output));
  _8_bit_register R_1 (.clk(and_2_out), .Input(Input), .ctrl(ctrl), .\output (R_1_output));
  _8_bit_register R_2 (.clk(and_3_out), .Input(Input), .ctrl(ctrl), .\output (R_2_output));
  _8_bit_register R_3 (.clk(and_4_out), .Input(Input), .ctrl(ctrl), .\output (R_3_output));
  Multiplexer #(.Selector_Bits(2), .Bits(8)) multiplexer_1 (
    .sel(RegisterSelection), .in_0(R_0_output), .in_1(R_1_output), .in_2(R_2_output), .in_3(R_3_output),
    .out(Output));

  // Notes on the sheet:
  //   ctrl: 00->Load
  //   01->Store
  //   10->Clear
  //   11->Set FF
  //   00->Load
  //   01->Store
  //   10->Clear
  //   11->Set FF
  //   Matthew's General Purpose Register Implementation
endmodule
