// Digital circuit SRAM-8bit-16address.dig as structural Verilog
module SRAM_8bit_16address (
  input  [3:0] Address_pin,
  input  clk,
  input  [7:0] Data_input,
  input  [1:0] Ctrl,
  output [7:0] Data_output
);

  wire and_1_out, and_2_out, and_3_out, and_4_out, and_5_out, and_6_out, and_7_out, and_8_out, and_9_out,
       and_10_out, and_11_out, and_12_out, and_13_out, and_14_out, and_15_out, and_16_out, decoder_1_out_0,
       decoder_1_out_1, decoder_1_out_2, decoder_1_out_3, decoder_1_out_4, decoder_1_out_5, decoder_1_out_6,
       decoder_1_out_7, decoder_1_out_8, decoder_1_out_9, decoder_1_out_10, decoder_1_out_11,
       decoder_1_out_12, decoder_1_out_13, decoder_1_out_14, decoder_1_out_15;
  wire [7:0] R_0_output, R_1_output, R_2_output, R_3_output, R_4_output, R_5_output, R_6_output, R_7_output,
       R_8_output, R_9_output, R_10_output, R_11_output, R_12_output, R_13_output, R_14_output, R_15_output;

  Decoder #(.Selector_Bits(4)) decoder_1 (
    .sel(Address_pin), .out_0(decoder_1_out_0), .out_1(decoder_1_out_1), .out_2(decoder_1_out_2),
    .out_3(decoder_1_out_3), .out_4(decoder_1_out_4), .out_5(decoder_1_out_5), .out_6(decoder_1_out_6),
    .out_7(decoder_1_out_7), .out_8(decoder_1_out_8), .out_9(decoder_1_out_9), .out_10(decoder_1_out_10),
    .out_11(decoder_1_out_11), .out_12(decoder_1_out_12), .out_13(decoder_1_out_13),
    .out_14(decoder_1_out_14), .out_15(decoder_1_out_15));
  and and_1 (and_1_out, clk, decoder_1_out_0);
  and and_2 (and_2_out, clk, decoder_1_out_1);
  and and_3 (and_3_out, clk, decoder_1_out_2);
  and and_4 (and_4_out, clk, decoder_1_out_3);
  and and_5 (and_5_out, clk, decoder_1_out_4);
  and and_6 (and_6_out, clk, decoder_1_out_5);
  and and_7 (and_7_out, clk, decoder_1_out_6);
  and and_8 (and_8_out, clk, decoder_1_out_7);
  and and_9 (and_9_out, clk, decoder_1_out_8);
  and and_10 (and_10_out, clk, decoder_1_out_9);
  and and_11 (and_11_out, clk, decoder_1_out_10);
  and and_12 (and_12_out, clk, decoder_1_out_11);
  and and_13 (and_13_out, clk, decoder_1_out_12);
  and and_14 (and_14_out, clk, decoder_1_out_13);
  and and_15 (and_15_out, clk, decoder_1_out_14);
  and and_16 (and_16_out, clk, decoder_1_out_15);
  _8_bit_register R_0 (.clk(and_1_out), .Input(Data_input), .ctrl(Ctrl), .\output (R_0_output));
  _8_bit_register R_1 (.clk(and_2_out), .Input(Data_input), .ctrl(Ctrl), .\output (R_1_output));
  _8_bit_register R_2 (.clk(and_3_out), .Input(Data_input), .ctrl(Ctrl), .\output (R_2_output));
  _8_bit_register R_3 (.clk(and_4_out), .Input(Data_input), .ctrl(Ctrl), .\output (R_3_output));
  _8_bit_register R_4 (.clk(and_5_out), .Input(Data_input), .ctrl(Ctrl), .\output (R_4_output));
  _8_bit_register R_5 (.clk(and_6_out), .Input(Data_input), .ctrl(Ctrl), .\output (R_5_output));
  _8_bit_register R_6 (.clk(and_7_out), .Input(Data_input), .ctrl(Ctrl), .\output (R_6_output));
  _8_bit_register R_7 (.clk(and_8_out), .Input(Data_input), .ctrl(Ctrl), .\output (R_7_output));
  _8_bit_register R_8 (.clk(and_9_out), .Input(Data_input), .ctrl(Ctrl), .\output (R_8_output));
  _8_bit_register R_9 (.clk(and_10_out), .Input(Data_input), .ctrl(Ctrl), .\output (R_9_output));
  _8_bit_register R_10 (.clk(and_11_out), .Input(Data_input), .ctrl(Ctrl), .\output (R_10_output));
  _8_bit_register R_11 (.clk(and_12_out), .Input(Data_input), .ctrl(Ctrl), .\output (R_11_output));
  _8_bit_register R_12 (.clk(and_13_out), .Input(Data_input), .ctrl(Ctrl), .\output (R_12_output));
  _8_bit_register R_13 (.clk(and_14_out), .Input(Data_input), .ctrl(Ctrl), .\output (R_13_output));
  _8_bit_register R_14 (.clk(and_15_out), .Input(Data_input), .ctrl(Ctrl), .\output (R_14_output));
  _8_bit_register R_15 (.clk(and_16_out), .Input(Data_input), .ctrl(Ctrl), .\output (R_15_output));
  Multiplexer #(.Selector_Bits(4), .Bits(8)) multiplexer_1 (
    .sel(Address_pin), .in_0(R_0_output), .in_1(R_1_output), .in_2(R_2_output), .in_3(R_3_output),
    .in_4(R_4_output), .in_5(R_5_output), .in_6(R_6_output), .in_7(R_7_output), .in_8(R_8_output),
    .in_9(R_9_output), .in_10(R_10_output), .in_11(R_11_output), .in_12(R_12_output), .in_13(R_13_output),
    .in_14(R_14_output), .in_15(R_15_output), .out(Data_output));

  // Notes on the sheet:
  //   Ctrl: 00->Load
  //   01->Store
  //   10->Clear
  //   11->Set FF
  //   Ctrl:
  //   00->Load
  //   01->Store
  //   10->Clear
  //   11->Set FF
  //   Matthew's 16 address 8-bit SRAM Implementation
endmodule
