// Digital circuit SRAM16bit.dig as structural Verilog
module SRAM16bit (
  input  [3:0] Address_pin,
  input  clk,
  input  [7:0] Data_input,
  input  [1:0] Ctrl,
  output [7:0] Data_output
);

  wire and_1_out, and_2_out, and_3_out, and_4_out, and_5_out, and_6_out, and_7_out, and_8_out, and_9_out,
       and_10_out, and_11_out, and_12_out, and_13_out, and_14_out, and_15_out, and_16_out, decoder_1_out_0,
       decoder_1_out_1, decoder_1_out_2, decoder_1_out_3, decoder_1_out_4, decoder_1_out_5, decoder_1_out_6,
       decoder_1_out_7, decoder_1_out_8, decoder_1_out_9, decoder_1_out_10, decoder_1_out_11,
       decoder_1_out_12, decoder_1_out_13, decoder_1_out_14, decoder_1_out_15;
  wire [7:0] _8_bit_register_1_output, _8_bit_register_2_output, _8_bit_register_3_output,
       _8_bit_register_4_output, _8_bit_register_5_output, _8_bit_register_6_output,
       _8_bit_register_7_output, _8_bit_register_8_output, _8_bit_register_9_output,
       _8_bit_register_10_output, _8_bit_register_11_output, _8_bit_register_12_output,
       _8_bit_register_13_output, _8_bit_register_14_output, _8_bit_register_15_output,
       _8_bit_register_16_output;

  Decoder #(.Selector_Bits(4)) decoder_1 (
    .sel(Address_pin), .out_0(decoder_1_out_0), .out_1(decoder_1_out_1), .out_2(decoder_1_out_2),
    .out_3(decoder_1_out_3), .out_4(decoder_1_out_4), .out_5(decoder_1_out_5), .out_6(decoder_1_out_6),
    .out_7(decoder_1_out_7), .out_8(decoder_1_out_8), .out_9(decoder_1_out_9), .out_10(decoder_1_out_10),
    .out_11(decoder_1_out_11), .out_12(decoder_1_out_12), .out_13(decoder_1_out_13),
    .out_14(decoder_1_out_14), .out_15(decoder_1_out_15));
  and and_1 (and_1_out, clk, decoder_1_out_0);
  and and_2 (and_2_out, clk, decoder_1_out_1);
  and and_3 (and_3_out, clk, decoder_1_out_2);
  and and_4 (and_4_out, clk, decoder_1_out_3);
  and and_5 (and_5_out, clk, decoder_1_out_4);
  and and_6 (and_6_out, clk, decoder_1_out_5);
  and and_7 (and_7_out, clk, decoder_1_out_6);
  and and_8 (and_8_out, clk, decoder_1_out_7);
  and and_9 (and_9_out, clk, decoder_1_out_8);
  and and_10 (and_10_out, clk, decoder_1_out_9);
  and and_11 (and_11_out, clk, decoder_1_out_10);
  and and_12 (and_12_out, clk, decoder_1_out_11);
  and and_13 (and_13_out, clk, decoder_1_out_12);
  and and_14 (and_14_out, clk, decoder_1_out_13);
  and and_15 (and_15_out, clk, decoder_1_out_14);
  and and_16 (and_16_out, clk, decoder_1_out_15);
  _8_bit_register _8_bit_register_1 (
    .clk(and_1_out), .Input(Data_input), .ctrl(Ctrl), .\output (_8_bit_register_1_output));
  _8_bit_register _8_bit_register_2 (
    .clk(and_2_out), .Input(Data_input), .ctrl(Ctrl), .\output (_8_bit_register_2_output));
  _8_bit_register _8_bit_register_3 (
    .clk(and_3_out), .Input(Data_input), .ctrl(Ctrl), .\output (_8_bit_register_3_output));
  _8_bit_register _8_bit_register_4 (
    .clk(and_4_out), .Input(Data_input), .ctrl(Ctrl), .\output (_8_bit_register_4_output));
  _8_bit_register _8_bit_register_5 (
    .clk(and_5_out), .Input(Data_input), .ctrl(Ctrl), .\output (_8_bit_register_5_output));
  _8_bit_register _8_bit_register_6 (
    .clk(and_6_out), .Input(Data_input), .ctrl(Ctrl), .\output (_8_bit_register_6_output));
  _8_bit_register _8_bit_register_7 (
    .clk(and_7_out), .Input(Data_input), .ctrl(Ctrl), .\output (_8_bit_register_7_output));
  _8_bit_register _8_bit_register_8 (
    .clk(and_8_out), .Input(Data_input), .ctrl(Ctrl), .\output (_8_bit_register_8_output));
  _8_bit_register _8_bit_register_9 (
    .clk(and_9_out), .Input(Data_input), .ctrl(Ctrl), .\output (_8_bit_register_9_output));
  _8_bit_register _8_bit_register_10 (
    .clk(and_10_out), .Input(Data_input), .ctrl(Ctrl), .\output (_8_bit_register_10_output));
  _8_bit_register _8_bit_register_11 (
    .clk(and_11_out), .Input(Data_input), .ctrl(Ctrl), .\output (_8_bit_register_11_output));
  _8_bit_register _8_bit_register_12 (
    .clk(and_12_out), .Input(Data_input), .ctrl(Ctrl), .\output (_8_bit_register_12_output));
  _8_bit_register _8_bit_register_13 (
    .clk(and_13_out), .Input(Data_input), .ctrl(Ctrl), .\output (_8_bit_register_13_output));
  _8_bit_register _8_bit_register_14 (
    .clk(and_14_out), .Input(Data_input), .ctrl(Ctrl), .\output (_8_bit_register_14_output));
  _8_bit_register _8_bit_register_15 (
    .clk(and_15_out), .Input(Data_input), .ctrl(Ctrl), .\output (_8_bit_register_15_output));
  _8_bit_register _8_bit_register_16 (
    .clk(and_16_out), .Input(Data_input), .ctrl(Ctrl), .\output (_8_bit_register_16_output));
  Multiplexer #(.Selector_Bits(4), .Bits(8)) multiplexer_1 (
    .sel(Address_pin), .in_0(_8_bit_register_1_output), .in_1(_8_bit_register_2_output),
    .in_2(_8_bit_register_3_output), .in_3(_8_bit_register_4_output), .in_4(_8_bit_register_5_output),
    .in_5(_8_bit_register_6_output), .in_6(_8_bit_register_7_output), .in_7(_8_bit_register_8_output),
    .in_8(_8_bit_register_9_output), .in_9(_8_bit_register_10_output), .in_10(_8_bit_register_11_output),
    .in_11(_8_bit_register_12_output), .in_12(_8_bit_register_13_output), .in_13(_8_bit_register_14_output),
    .in_14(_8_bit_register_15_output), .in_15(_8_bit_register_16_output), .out(Data_output));

  // Notes on the sheet:
  //   Ctrl: 00->Load
  //   01->Store
  //   10->Clear
  //   11->Set FF
  //   Ctrl:
  //   00->Load
  //   01->Store
  //   10->Clear
  //   11->Set FF
  //   Matthew's 16 bit SRAM Implementation
endmodule
